// Logisim project jiw159_lab7.circ as structural Verilog: 1 circuit, main circuit main
module main (
  input  [3:0] A,
  input  [3:0] B,
  input  sub
);

  wire adder_1_cout, AM, M_M, M_O, not_2_p2, not_3_p2, not_4_out, SOV, UOV, xor_2_out;
  wire [2:0] multiplexer_1_out, O;
  wire [3:0] not_1_p2;

  // NOT_Gate #(.width(4)) not_1: pin names not known; wires that end beside it: B, not_1_p2
  Multiplexer #(.width(4)) multiplexer_1 (
    .in0(B), .in1(not_1_p2), .out({M_M, multiplexer_1_out}), .sel(sub));  // open: en
  // Probe on A
  // Probe on B
  // Probe on {M_O, O}
  LED led_1 (.in(UOV));
  Adder #(.width(4)) adder_1 (.a(A), .b({M_M, multiplexer_1_out}), .out({M_O, O}), .cin(sub), .cout(adder_1_cout));
  // NOT_Gate not_2: pin names not known; wires that end beside it: adder_1_cout, not_2_p2
  Multiplexer multiplexer_2 (.in0(adder_1_cout), .in1(not_2_p2), .out(UOV), .sel(sub));  // open: en
  // Probe on A
  // Probe on B
  // Probe on {M_O, O}
  LED led_2 (.in(SOV));
  // NOT_Gate not_3: pin names not known; wires that end beside it: AM, not_3_p2
  buf xor_1 (AM, A[3]);  // XOR_Gate
  not not_4 (not_4_out, AM);
  Multiplexer multiplexer_3 (.in0(not_4_out), .in1(xor_2_out), .out(SOV), .sel(not_3_p2));  // open: en
  xor xor_2 (xor_2_out, M_O, A[3]);

  // Other names for the same wires on the sheet: M_A = A[3]; O[3] = M_O
endmodule
